# Fritzing sketch wiring (saved by Fritzing 0.8.7b)

parts:
  Part1 = Arduino Nano (Rev3.0)
  Transceiver1 = nRF24L01 [package=module]
  Raspberry_Pi_B_rev1 = Raspberry Pi B rev2
  L298N1 = L298N DC motor driver
  BAT1 = BC9VPC [package=bc9vpc]
  M1 = DC Motor  # not connected
  Transceiver2 = nRF24L01 [package=module]

nets:
  N1: Part1.D2, L298N1.ENB
  N2: Part1.D3, L298N1.IN4
  N3: Part1.D4, L298N1.IN3
  N4: Part1.D9, Transceiver1.CE
  N5: Part1.D10, Transceiver1.CSN
  N6: Part1.D11/MOSI, Transceiver1.MOSI
  N7: Part1.D12/MISO, Transceiver1.MISO
  VIN: Part1.VIN, L298N1.12V, BAT1.V-
  GND: Part1.GND, Transceiver1.GND, L298N1.GND, BAT1.V+
  3V3: Part1.3V3, Transceiver1.VCC
  N8: Part1.D13/SCK, Transceiver1.SCK
  3V3_2: Raspberry_Pi_B_rev1.3V3, Transceiver2.VCC
  GND_2: Raspberry_Pi_B_rev1.GND, Transceiver2.GND
  N9: Raspberry_Pi_B_rev1.GPIO_10, Transceiver2.MOSI
  N10: Raspberry_Pi_B_rev1.GPIO_9, Transceiver2.MISO
  N11: Raspberry_Pi_B_rev1.GPIO_25, Transceiver2.CE
  N12: Raspberry_Pi_B_rev1.GPIO_11, Transceiver2.SCK
  N13: Raspberry_Pi_B_rev1.GPIO_8, Transceiver2.CSN

custom parts:
  nRF24L01: nRF24L01 module
  L298N DC motor driver: 2x DC motor driver with 78M05 positive voltage regulator (7..35 V) L298N: max 46 V, 2 A Set 5 V Enable jumper to enable 5 V regultor (needed for the L298N) and +5 V output at screw terminal or supply external +5 V at screw terminal Set ENA and/or ENB to +5 V to enable motor permanently or supply ENA and/or ENB with PWM signal IN1 and IN2 set rotation directory for motor A (OUT1/OUT2) IN2 and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
